# Fritzing sketch neo-controller (saved by Fritzing 1.0.3b)
breadboards: 2

parts:
  U1 = Mini-360 DC-DC Buck converter [package=THT]
  Mod1 = seeeduino-xiao
  D1 = Schottky Diode [part_number=1N5817 package="300 mil [THT]"]
  D2 = Schottky Diode [part_number=1N5817 package="300 mil [THT]"]
  S1 = Pushbutton [package="[THT]"]
  S2 = Pushbutton [package="[THT]"]
  S3 = Pushbutton [package="[THT]"]
  S4 = Pushbutton [package="[THT]"]
  S5 = Pushbutton [package="[THT]"]
  S6 = Pushbutton [package="[THT]"]
  Mod2 = seeeduino-xiao
  D3 = Schottky Diode [part_number=1N5817 package="300 mil [THT]"]

nets:
  N1: U1.IN-, Mod1.GND
  N2: U1.IN+, D1.cathode
  N3: U1.OUT+, D2.anode, D3.anode
  N4: U1.OUT-, S1.Pin_1, S1.Pin_2, S2.Pin_1, S2.Pin_2, S3.Pin_1, S3.Pin_2, S4.Pin_1, S4.Pin_2, S5.Pin_1, S5.Pin_2, S6.Pin_1, S6.Pin_2, Mod2.GND
  N5: Mod1.D4, Mod2.D4
  N6: Mod1.D5, Mod2.D5
  N7: Mod1.5V, D2.cathode
  N8: S1.Pin_3, S1.Pin_4, Mod2.D1
  N9: S2.Pin_3, S2.Pin_4, Mod2.D3
  N10: S3.Pin_3, S3.Pin_4, Mod2.D2
  N11: S4.Pin_3, S4.Pin_4
  N12: S5.Pin_3, S5.Pin_4, Mod2.D10
  N13: S6.Pin_3, S6.Pin_4, Mod2.D9
  N14: Mod2.5V, D3.cathode

notes:
  V-
  V+
  5v
  SDA
  SCL
  D

custom parts:
  Mini-360 DC-DC Buck converter: Mini-360 DC-DC Buck converter. Tiny buck step down voltage converter, input voltage 4.75 to 23V output 1 to 17V adjustable. Available from ebay and the like.
  seeeduino-xiao: Seeeduino XIAO processor board.
